// Digital circuit And.dig as structural Verilog
module And (
  input  a,
  input  b
);

  wire nand_1_out, not_1_out;

  nand nand_1 (nand_1_out, a, b);
  not not_1 (not_1_out, nand_1_out);
  LED led_1 (.in(not_1_out));
endmodule
