// Digital circuit And16.dig as structural Verilog
module And16 (
  input  [15:0] a,
  input  [15:0] b,
  output [15:0] out
);

  wire and_1_out, and_2_out, and_3_out, and_4_out, and_5_out, and_6_out, and_7_out, and_8_out, and_9_out,
       and_10_out, and_11_out, and_12_out, and_13_out, and_14_out, and_15_out, and_16_out, bussplitter_1_d0,
       bussplitter_1_d1, bussplitter_1_d2, bussplitter_1_d3, bussplitter_1_d4, bussplitter_1_d5,
       bussplitter_1_d6, bussplitter_1_d7, bussplitter_1_d8, bussplitter_1_d9, bussplitter_1_d10,
       bussplitter_1_d11, bussplitter_1_d12, bussplitter_1_d13, bussplitter_1_d14, bussplitter_1_d15,
       bussplitter_2_d0, bussplitter_2_d1, bussplitter_2_d2, bussplitter_2_d3, bussplitter_2_d4,
       bussplitter_2_d5, bussplitter_2_d6, bussplitter_2_d7, bussplitter_2_d8, bussplitter_2_d9,
       bussplitter_2_d10, bussplitter_2_d11, bussplitter_2_d12, bussplitter_2_d13, bussplitter_2_d14,
       bussplitter_2_d15, dipswitch_1_out, dipswitch_2_out, dipswitch_3_out;

  BusSplitter #(.Bits(16)) bussplitter_1 (
    .D(b), .OE(dipswitch_1_out), .D0(bussplitter_1_d0), .D1(bussplitter_1_d1), .D2(bussplitter_1_d2),
    .D3(bussplitter_1_d3), .D4(bussplitter_1_d4), .D5(bussplitter_1_d5), .D6(bussplitter_1_d6),
    .D7(bussplitter_1_d7), .D8(bussplitter_1_d8), .D9(bussplitter_1_d9), .D10(bussplitter_1_d10),
    .D11(bussplitter_1_d11), .D12(bussplitter_1_d12), .D13(bussplitter_1_d13), .D14(bussplitter_1_d14),
    .D15(bussplitter_1_d15));
  DipSwitch #(.dipDefault("true")) dipswitch_1 (.out(dipswitch_1_out));
  BusSplitter #(.Bits(16)) bussplitter_2 (
    .D(a), .OE(dipswitch_2_out), .D0(bussplitter_2_d0), .D1(bussplitter_2_d1), .D2(bussplitter_2_d2),
    .D3(bussplitter_2_d3), .D4(bussplitter_2_d4), .D5(bussplitter_2_d5), .D6(bussplitter_2_d6),
    .D7(bussplitter_2_d7), .D8(bussplitter_2_d8), .D9(bussplitter_2_d9), .D10(bussplitter_2_d10),
    .D11(bussplitter_2_d11), .D12(bussplitter_2_d12), .D13(bussplitter_2_d13), .D14(bussplitter_2_d14),
    .D15(bussplitter_2_d15));
  DipSwitch #(.dipDefault("true")) dipswitch_2 (.out(dipswitch_2_out));
  and and_1 (and_1_out, bussplitter_2_d0, bussplitter_1_d0);
  and and_2 (and_2_out, bussplitter_2_d1, bussplitter_1_d1);
  and and_3 (and_3_out, bussplitter_2_d2, bussplitter_1_d2);
  and and_4 (and_4_out, bussplitter_2_d3, bussplitter_1_d3);
  and and_5 (and_5_out, bussplitter_2_d4, bussplitter_1_d4);
  and and_6 (and_6_out, bussplitter_2_d5, bussplitter_1_d5);
  and and_7 (and_7_out, bussplitter_2_d6, bussplitter_1_d6);
  and and_8 (and_8_out, bussplitter_2_d7, bussplitter_1_d7);
  and and_9 (and_9_out, bussplitter_2_d8, bussplitter_1_d8);
  and and_10 (and_10_out, bussplitter_2_d9, bussplitter_1_d9);
  and and_11 (and_11_out, bussplitter_2_d10, bussplitter_1_d10);
  and and_12 (and_12_out, bussplitter_2_d11, bussplitter_1_d11);
  and and_13 (and_13_out, bussplitter_2_d12, bussplitter_1_d12);
  and and_14 (and_14_out, bussplitter_2_d13, bussplitter_1_d13);
  and and_15 (and_15_out, bussplitter_2_d14, bussplitter_1_d14);
  and and_16 (and_16_out, bussplitter_2_d15, bussplitter_1_d15);
  BusSplitter #(.Bits(16)) bussplitter_3 (
    .D(out), .OE(dipswitch_3_out), .D0(and_1_out), .D1(and_2_out), .D2(and_3_out), .D3(and_4_out),
    .D4(and_5_out), .D5(and_6_out), .D6(and_7_out), .D7(and_8_out), .D8(and_9_out), .D9(and_10_out),
    .D10(and_11_out), .D11(and_12_out), .D12(and_13_out), .D13(and_14_out), .D14(and_15_out), .D15(and_16_out));
  DipSwitch dipswitch_3 (.out(dipswitch_3_out));
endmodule
