// Digital circuit DMux4Way.dig as structural Verilog
module DMux4Way (
  input  in,
  input  [1:0] sel,
  output a,
  output c,
  output b,
  output d
);

  wire bussplitter_1_d0, bussplitter_1_d1, dipswitch_1_out, dmux_1_a, dmux_1_b;

  BusSplitter #(.Bits(2)) bussplitter_1 (.D(sel), .OE(dipswitch_1_out), .D0(bussplitter_1_d0), .D1(bussplitter_1_d1));
  DipSwitch #(.dipDefault("true")) dipswitch_1 (.out(dipswitch_1_out));
  Dmux dmux_1 (.in(in), .sel(bussplitter_1_d0), .a(dmux_1_a), .b(dmux_1_b));
  Dmux dmux_2 (.in(dmux_1_a), .sel(bussplitter_1_d1), .a(a), .b(c));
  Dmux dmux_3 (.in(dmux_1_b), .sel(bussplitter_1_d1), .a(b), .b(d));
endmodule
