// Digital circuit DMux8Way.dig as structural Verilog
module DMux8Way (
  input  in,
  input  sel_pin0,
  input  [1:0] sel_pin1_and_2
);

  wire demultiplexer_1_out_0, demultiplexer_1_out_1, demultiplexer_2_out_0, demultiplexer_2_out_1,
       demultiplexer_2_out_2, demultiplexer_2_out_3, demultiplexer_3_out_0, demultiplexer_3_out_1,
       demultiplexer_3_out_2, demultiplexer_3_out_3;

  Demultiplexer demultiplexer_1 (.sel(sel_pin0), .in(in), .out_0(demultiplexer_1_out_0), .out_1(demultiplexer_1_out_1));
  Demultiplexer #(.Selector_Bits(2)) demultiplexer_2 (
    .sel(sel_pin1_and_2), .in(demultiplexer_1_out_0), .out_0(demultiplexer_2_out_0),
    .out_1(demultiplexer_2_out_1), .out_2(demultiplexer_2_out_2), .out_3(demultiplexer_2_out_3));
  Demultiplexer #(.Selector_Bits(2)) demultiplexer_3 (
    .sel(sel_pin1_and_2), .in(demultiplexer_1_out_1), .out_0(demultiplexer_3_out_0),
    .out_1(demultiplexer_3_out_1), .out_2(demultiplexer_3_out_2), .out_3(demultiplexer_3_out_3));
  LED led_1 (.in(demultiplexer_2_out_0));
  LED led_2 (.in(demultiplexer_3_out_0));
  LED led_3 (.in(demultiplexer_2_out_1));
  LED led_4 (.in(demultiplexer_2_out_2));
  LED led_5 (.in(demultiplexer_3_out_1));
  LED led_6 (.in(demultiplexer_3_out_2));
  LED led_7 (.in(demultiplexer_2_out_3));
  LED led_8 (.in(demultiplexer_3_out_3));
endmodule
