// Digital circuit Dmux.dig as structural Verilog
module Dmux (
  input  in,
  input  sel,
  output a,
  output b
);

  wire false_out;

  Button false (.out(false_out));
  Multiplexer multiplexer_1 (.sel(sel), .in_0(in), .in_1(false_out), .out(a));
  Multiplexer multiplexer_2 (.sel(sel), .in_0(false_out), .in_1(in), .out(b));
endmodule
