// Digital circuit Mux.dig as structural Verilog
module Mux (
  input  A,
  input  B,
  input  SEL,
  output Y
);

  wire and_1_out, and_2_out, not_1_out;

  not not_1 (not_1_out, SEL);
  and and_1 (and_1_out, A, not_1_out);
  and and_2 (and_2_out, B, SEL);
  or or_1 (Y, and_1_out, and_2_out);
endmodule
