// Digital circuit Mux16.dig as structural Verilog
module Mux16 (
  input  sel,
  input  [15:0] b,
  input  [15:0] b_2,
  output [15:0] out
);

  wire bussplitter_1_d0, bussplitter_1_d1, bussplitter_1_d2, bussplitter_1_d3, bussplitter_1_d4,
       bussplitter_1_d5, bussplitter_1_d6, bussplitter_1_d7, bussplitter_1_d8, bussplitter_1_d9,
       bussplitter_1_d10, bussplitter_1_d11, bussplitter_1_d12, bussplitter_1_d13, bussplitter_1_d14,
       bussplitter_1_d15, bussplitter_2_d0, bussplitter_2_d1, bussplitter_2_d2, bussplitter_2_d3,
       bussplitter_2_d4, bussplitter_2_d5, bussplitter_2_d6, bussplitter_2_d7, bussplitter_2_d8,
       bussplitter_2_d9, bussplitter_2_d10, bussplitter_2_d11, bussplitter_2_d12, bussplitter_2_d13,
       bussplitter_2_d14, bussplitter_2_d15, dipswitch_1_out, dipswitch_2_out, dipswitch_3_out, mux_1_y,
       mux_2_y, mux_3_y, mux_4_y, mux_5_y, mux_6_y, mux_7_y, mux_8_y, mux_9_y, mux_10_y, mux_11_y, mux_12_y,
       mux_13_y, mux_14_y, mux_15_y, mux_16_y;

  BusSplitter #(.Bits(16)) bussplitter_1 (
    .D(b_2), .OE(dipswitch_1_out), .D0(bussplitter_1_d0), .D1(bussplitter_1_d1), .D2(bussplitter_1_d2),
    .D3(bussplitter_1_d3), .D4(bussplitter_1_d4), .D5(bussplitter_1_d5), .D6(bussplitter_1_d6),
    .D7(bussplitter_1_d7), .D8(bussplitter_1_d8), .D9(bussplitter_1_d9), .D10(bussplitter_1_d10),
    .D11(bussplitter_1_d11), .D12(bussplitter_1_d12), .D13(bussplitter_1_d13), .D14(bussplitter_1_d14),
    .D15(bussplitter_1_d15));
  DipSwitch #(.dipDefault("true")) dipswitch_1 (.out(dipswitch_1_out));
  BusSplitter #(.Bits(16)) bussplitter_2 (
    .D(b), .OE(dipswitch_2_out), .D0(bussplitter_2_d0), .D1(bussplitter_2_d1), .D2(bussplitter_2_d2),
    .D3(bussplitter_2_d3), .D4(bussplitter_2_d4), .D5(bussplitter_2_d5), .D6(bussplitter_2_d6),
    .D7(bussplitter_2_d7), .D8(bussplitter_2_d8), .D9(bussplitter_2_d9), .D10(bussplitter_2_d10),
    .D11(bussplitter_2_d11), .D12(bussplitter_2_d12), .D13(bussplitter_2_d13), .D14(bussplitter_2_d14),
    .D15(bussplitter_2_d15));
  DipSwitch #(.dipDefault("true")) dipswitch_2 (.out(dipswitch_2_out));
  Mux mux_1 (.A(bussplitter_2_d0), .B(bussplitter_1_d0), .SEL(sel), .Y(mux_1_y));
  Mux mux_2 (.A(bussplitter_2_d1), .B(bussplitter_1_d1), .SEL(sel), .Y(mux_2_y));
  Mux mux_3 (.A(bussplitter_2_d2), .B(bussplitter_1_d2), .SEL(sel), .Y(mux_3_y));
  Mux mux_4 (.A(bussplitter_2_d3), .B(bussplitter_1_d3), .SEL(sel), .Y(mux_4_y));
  Mux mux_5 (.A(bussplitter_2_d4), .B(bussplitter_1_d4), .SEL(sel), .Y(mux_5_y));
  Mux mux_6 (.A(bussplitter_2_d5), .B(bussplitter_1_d5), .SEL(sel), .Y(mux_6_y));
  Mux mux_7 (.A(bussplitter_2_d6), .B(bussplitter_1_d6), .SEL(sel), .Y(mux_7_y));
  Mux mux_8 (.A(bussplitter_2_d7), .B(bussplitter_1_d7), .SEL(sel), .Y(mux_8_y));
  Mux mux_9 (.A(bussplitter_2_d8), .B(bussplitter_1_d8), .SEL(sel), .Y(mux_9_y));
  Mux mux_10 (.A(bussplitter_2_d9), .B(bussplitter_1_d9), .SEL(sel), .Y(mux_10_y));
  Mux mux_11 (.A(bussplitter_2_d10), .B(bussplitter_1_d10), .SEL(sel), .Y(mux_11_y));
  Mux mux_12 (.A(bussplitter_2_d11), .B(bussplitter_1_d11), .SEL(sel), .Y(mux_12_y));
  Mux mux_13 (.A(bussplitter_2_d12), .B(bussplitter_1_d12), .SEL(sel), .Y(mux_13_y));
  Mux mux_14 (.A(bussplitter_2_d13), .B(bussplitter_1_d13), .SEL(sel), .Y(mux_14_y));
  Mux mux_15 (.A(bussplitter_2_d14), .B(bussplitter_1_d14), .SEL(sel), .Y(mux_15_y));
  Mux mux_16 (.A(bussplitter_2_d15), .B(bussplitter_1_d15), .SEL(sel), .Y(mux_16_y));
  BusSplitter #(.Bits(16)) bussplitter_3 (
    .D(out), .OE(dipswitch_3_out), .D0(mux_1_y), .D1(mux_2_y), .D2(mux_3_y), .D3(mux_4_y), .D4(mux_5_y),
    .D5(mux_6_y), .D6(mux_7_y), .D7(mux_8_y), .D8(mux_9_y), .D9(mux_10_y), .D10(mux_11_y), .D11(mux_12_y),
    .D12(mux_13_y), .D13(mux_14_y), .D14(mux_15_y), .D15(mux_16_y));
  DipSwitch dipswitch_3 (.out(dipswitch_3_out));
endmodule
