// Digital circuit Mux4Way16.dig as structural Verilog
module Mux4Way16 (
  input  [15:0] A___16_bits,
  input  [15:0] B___16_bits,
  input  [15:0] C___16_bits,
  input  [15:0] D___16_bits,
  input  [15:0] SEL0___16_bits,
  input  [15:0] SEL1___16_bits,
  output [15:0] Y___16_bits
);

  wire [15:0] and_1_out, and_2_out, and_3_out, and_4_out, not_1_out, not_2_out;

  assign not_1_out = ~SEL0___16_bits;  // Not not_1, 16 bits wide
  assign not_2_out = ~SEL1___16_bits;  // Not not_2, 16 bits wide
  assign and_1_out = A___16_bits & not_1_out & not_2_out;  // And and_1, 16 bits wide
  assign and_2_out = B___16_bits & SEL0___16_bits & not_2_out;  // And and_2, 16 bits wide
  assign and_3_out = C___16_bits & not_1_out & SEL1___16_bits;  // And and_3, 16 bits wide
  assign and_4_out = D___16_bits & SEL0___16_bits & SEL1___16_bits;  // And and_4, 16 bits wide
  assign Y___16_bits = and_1_out | and_2_out | and_3_out | and_4_out;  // Or or_1, 16 bits wide
endmodule
