// Digital circuit Mux8Way16.dig as structural Verilog
module Mux8Way16 (
  input  [15:0] a,
  input  [15:0] b,
  input  [15:0] c,
  input  [15:0] d,
  input  [15:0] e,
  input  [15:0] f,
  input  [15:0] g,
  input  [15:0] h,
  input  [2:0] sel,
  output [15:0] out
);

  wire bussplitter_1_d0, bussplitter_1_d1, bussplitter_2_d2, dipswitch_1_out, dipswitch_2_out;
  wire [1:0] bussplitter_1_d;
  wire [15:0] mux4way16_1_out, mux4way16_2_out;

  Mux4Way16 mux4way16_1 (.a(a), .c(b), .b(c), .d(d), .sel(bussplitter_1_d), .out(mux4way16_1_out));
  Mux4Way16 mux4way16_2 (.a(e), .c(f), .b(g), .d(h), .sel(bussplitter_1_d), .out(mux4way16_2_out));
  BusSplitter #(.Bits(2)) bussplitter_1 (
    .D(bussplitter_1_d), .OE(dipswitch_1_out), .D0(bussplitter_1_d0), .D1(bussplitter_1_d1));
  DipSwitch dipswitch_1 (.out(dipswitch_1_out));
  BusSplitter #(.Bits(3)) bussplitter_2 (
    .D(sel), .OE(dipswitch_2_out), .D0(bussplitter_1_d0), .D1(bussplitter_1_d1), .D2(bussplitter_2_d2));
  DipSwitch #(.dipDefault("true")) dipswitch_2 (.out(dipswitch_2_out));
  // Mux16 mux16_1: pin names not known; wires that end beside it: bussplitter_2_d2, mux4way16_1_out, mux4way16_2_out, out
endmodule
