// Digital circuit Not16.dig as structural Verilog
module Not16 (
  input  [15:0] in,
  output [15:0] out
);

  wire bussplitter_1_d0, bussplitter_1_d1, bussplitter_1_d2, bussplitter_1_d3, bussplitter_1_d4,
       bussplitter_1_d5, bussplitter_1_d6, bussplitter_1_d7, bussplitter_1_d8, bussplitter_1_d9,
       bussplitter_1_d10, bussplitter_1_d11, bussplitter_1_d12, bussplitter_1_d13, bussplitter_1_d14,
       bussplitter_1_d15, dipswitch_1_out, dipswitch_2_out, nand_1_out, nand_2_out, nand_3_out, nand_4_out,
       nand_5_out, nand_6_out, nand_7_out, nand_8_out, nand_9_out, nand_10_out, nand_11_out, nand_12_out,
       nand_13_out, nand_14_out, nand_15_out, nand_16_out;

  BusSplitter #(.Bits(16)) bussplitter_1 (
    .D(in), .OE(dipswitch_1_out), .D0(bussplitter_1_d0), .D1(bussplitter_1_d1), .D2(bussplitter_1_d2),
    .D3(bussplitter_1_d3), .D4(bussplitter_1_d4), .D5(bussplitter_1_d5), .D6(bussplitter_1_d6),
    .D7(bussplitter_1_d7), .D8(bussplitter_1_d8), .D9(bussplitter_1_d9), .D10(bussplitter_1_d10),
    .D11(bussplitter_1_d11), .D12(bussplitter_1_d12), .D13(bussplitter_1_d13), .D14(bussplitter_1_d14),
    .D15(bussplitter_1_d15));
  DipSwitch #(.dipDefault("true")) dipswitch_1 (.out(dipswitch_1_out));
  nand nand_1 (nand_1_out, bussplitter_1_d0, bussplitter_1_d0);
  nand nand_2 (nand_2_out, bussplitter_1_d1, bussplitter_1_d1);
  nand nand_3 (nand_3_out, bussplitter_1_d2, bussplitter_1_d2);
  nand nand_4 (nand_4_out, bussplitter_1_d3, bussplitter_1_d3);
  nand nand_5 (nand_5_out, bussplitter_1_d4, bussplitter_1_d4);
  nand nand_6 (nand_6_out, bussplitter_1_d5, bussplitter_1_d5);
  nand nand_7 (nand_7_out, bussplitter_1_d6, bussplitter_1_d6);
  nand nand_8 (nand_8_out, bussplitter_1_d7, bussplitter_1_d7);
  nand nand_9 (nand_9_out, bussplitter_1_d8, bussplitter_1_d8);
  nand nand_10 (nand_10_out, bussplitter_1_d9, bussplitter_1_d9);
  nand nand_11 (nand_11_out, bussplitter_1_d10, bussplitter_1_d10);
  nand nand_12 (nand_12_out, bussplitter_1_d11, bussplitter_1_d11);
  nand nand_13 (nand_13_out, bussplitter_1_d12, bussplitter_1_d12);
  nand nand_14 (nand_14_out, bussplitter_1_d13, bussplitter_1_d13);
  nand nand_15 (nand_15_out, bussplitter_1_d14, bussplitter_1_d14);
  nand nand_16 (nand_16_out, bussplitter_1_d15, bussplitter_1_d15);
  BusSplitter #(.Bits(16)) bussplitter_2 (
    .D(out), .OE(dipswitch_2_out), .D0(nand_1_out), .D1(nand_2_out), .D2(nand_3_out), .D3(nand_4_out),
    .D4(nand_5_out), .D5(nand_6_out), .D6(nand_7_out), .D7(nand_8_out), .D8(nand_9_out), .D9(nand_10_out),
    .D10(nand_11_out), .D11(nand_12_out), .D12(nand_13_out), .D13(nand_14_out), .D14(nand_15_out),
    .D15(nand_16_out));
  DipSwitch dipswitch_2 (.out(dipswitch_2_out));
endmodule
