// Digital circuit Or.dig as structural Verilog
module Or (
  input  a,
  input  b
);

  wire and_1_out, not_1_out, not_2_out, not_3_out;

  not not_1 (not_1_out, a);
  not not_2 (not_2_out, b);
  and and_1 (and_1_out, not_1_out, not_2_out);
  not not_3 (not_3_out, and_1_out);
  LED led_1 (.in(not_3_out));
endmodule
