// Digital circuit Or16.dig as structural Verilog
module Or16 (
  input  [15:0] a,
  input  [15:0] b,
  output [15:0] out
);

  wire bussplitter_1_d0, bussplitter_1_d1, bussplitter_1_d2, bussplitter_1_d3, bussplitter_1_d4,
       bussplitter_1_d5, bussplitter_1_d6, bussplitter_1_d7, bussplitter_1_d8, bussplitter_1_d9,
       bussplitter_1_d10, bussplitter_1_d11, bussplitter_1_d12, bussplitter_1_d13, bussplitter_1_d14,
       bussplitter_1_d15, bussplitter_2_d0, bussplitter_2_d1, bussplitter_2_d2, bussplitter_2_d3,
       bussplitter_2_d4, bussplitter_2_d5, bussplitter_2_d6, bussplitter_2_d7, bussplitter_2_d8,
       bussplitter_2_d9, bussplitter_2_d10, bussplitter_2_d11, bussplitter_2_d12, bussplitter_2_d13,
       bussplitter_2_d14, bussplitter_2_d15, dipswitch_1_out, dipswitch_2_out, dipswitch_3_out, or_1_out,
       or_2_out, or_3_out, or_4_out, or_5_out, or_6_out, or_7_out, or_8_out, or_9_out, or_10_out, or_11_out,
       or_12_out, or_13_out, or_14_out, or_15_out, or_16_out;

  BusSplitter #(.Bits(16)) bussplitter_1 (
    .D(b), .OE(dipswitch_1_out), .D0(bussplitter_1_d0), .D1(bussplitter_1_d1), .D2(bussplitter_1_d2),
    .D3(bussplitter_1_d3), .D4(bussplitter_1_d4), .D5(bussplitter_1_d5), .D6(bussplitter_1_d6),
    .D7(bussplitter_1_d7), .D8(bussplitter_1_d8), .D9(bussplitter_1_d9), .D10(bussplitter_1_d10),
    .D11(bussplitter_1_d11), .D12(bussplitter_1_d12), .D13(bussplitter_1_d13), .D14(bussplitter_1_d14),
    .D15(bussplitter_1_d15));
  DipSwitch #(.dipDefault("true")) dipswitch_1 (.out(dipswitch_1_out));
  BusSplitter #(.Bits(16)) bussplitter_2 (
    .D(a), .OE(dipswitch_2_out), .D0(bussplitter_2_d0), .D1(bussplitter_2_d1), .D2(bussplitter_2_d2),
    .D3(bussplitter_2_d3), .D4(bussplitter_2_d4), .D5(bussplitter_2_d5), .D6(bussplitter_2_d6),
    .D7(bussplitter_2_d7), .D8(bussplitter_2_d8), .D9(bussplitter_2_d9), .D10(bussplitter_2_d10),
    .D11(bussplitter_2_d11), .D12(bussplitter_2_d12), .D13(bussplitter_2_d13), .D14(bussplitter_2_d14),
    .D15(bussplitter_2_d15));
  DipSwitch #(.dipDefault("true")) dipswitch_2 (.out(dipswitch_2_out));
  or or_1 (or_1_out, bussplitter_2_d0, bussplitter_1_d0);
  or or_2 (or_2_out, bussplitter_2_d1, bussplitter_1_d1);
  or or_3 (or_3_out, bussplitter_2_d2, bussplitter_1_d2);
  or or_4 (or_4_out, bussplitter_2_d3, bussplitter_1_d3);
  or or_5 (or_5_out, bussplitter_2_d4, bussplitter_1_d4);
  or or_6 (or_6_out, bussplitter_2_d5, bussplitter_1_d5);
  or or_7 (or_7_out, bussplitter_2_d6, bussplitter_1_d6);
  or or_8 (or_8_out, bussplitter_2_d7, bussplitter_1_d7);
  or or_9 (or_9_out, bussplitter_2_d8, bussplitter_1_d8);
  or or_10 (or_10_out, bussplitter_2_d9, bussplitter_1_d9);
  or or_11 (or_11_out, bussplitter_2_d10, bussplitter_1_d10);
  or or_12 (or_12_out, bussplitter_2_d11, bussplitter_1_d11);
  or or_13 (or_13_out, bussplitter_2_d12, bussplitter_1_d12);
  or or_14 (or_14_out, bussplitter_2_d13, bussplitter_1_d13);
  or or_15 (or_15_out, bussplitter_2_d14, bussplitter_1_d14);
  or or_16 (or_16_out, bussplitter_2_d15, bussplitter_1_d15);
  BusSplitter #(.Bits(16)) bussplitter_3 (
    .D(out), .OE(dipswitch_3_out), .D0(or_1_out), .D1(or_2_out), .D2(or_3_out), .D3(or_4_out), .D4(or_5_out),
    .D5(or_6_out), .D6(or_7_out), .D7(or_8_out), .D8(or_9_out), .D9(or_10_out), .D10(or_11_out),
    .D11(or_12_out), .D12(or_13_out), .D13(or_14_out), .D14(or_15_out), .D15(or_16_out));
  DipSwitch dipswitch_3 (.out(dipswitch_3_out));
endmodule
