// Digital circuit Or8Way.dig as structural Verilog
module Or8Way (
  input  [7:0] in,
  output out
);

  wire bussplitter_1_d0, bussplitter_1_d1, bussplitter_1_d2, bussplitter_1_d3, bussplitter_1_d4,
       bussplitter_1_d5, bussplitter_1_d6, bussplitter_1_d7, dipswitch_1_out, or_1_out, or_2_out, or_3_out,
       or_4_out, or_5_out, or_6_out;

  BusSplitter #(.Bits(8)) bussplitter_1 (
    .D(in), .OE(dipswitch_1_out), .D0(bussplitter_1_d0), .D1(bussplitter_1_d1), .D2(bussplitter_1_d2),
    .D3(bussplitter_1_d3), .D4(bussplitter_1_d4), .D5(bussplitter_1_d5), .D6(bussplitter_1_d6),
    .D7(bussplitter_1_d7));
  DipSwitch #(.dipDefault("true")) dipswitch_1 (.out(dipswitch_1_out));
  or or_1 (or_1_out, bussplitter_1_d0, bussplitter_1_d1);
  or or_2 (or_2_out, or_1_out, bussplitter_1_d2);
  or or_3 (or_3_out, or_2_out, bussplitter_1_d3);
  or or_4 (or_4_out, or_3_out, bussplitter_1_d4);
  or or_5 (or_5_out, or_4_out, bussplitter_1_d5);
  or or_6 (or_6_out, or_5_out, bussplitter_1_d6);
  or or_7 (out, or_6_out, bussplitter_1_d7);
endmodule
